# Fritzing sketch desk-droid (saved by Fritzing 1.0.6)
breadboards: 1

parts:
  A1 = ESP32-S3 supermini
  OLED_I2C1 = OLED 128x64 I2C Monochrome Display
  SG1 = Buzzer 12mm [part_number=COM-07950 package=buzzer-12mm-ns]
  Sensor1 = TTP223B Capacitive Touch Sensor Module
  Mod2 = KY-015 Temperature & Humidity Sensor Module [package="Breakout board"]

nets:
  N1: A1.Pin_33, Mod2.S
  N2: A1.Pin_34, Sensor1.SIG
  N3: A1.Pin_35, SG1.1
  N4: A1.Pin_36, OLED_I2C1.SDA
  N5: A1.Pin_37, OLED_I2C1.SCK
  VDD: A1.Pin_38, OLED_I2C1.VDD, Sensor1.VCC, Mod2.Vin
  GND: A1.Pin_39, OLED_I2C1.GND, SG1.2, Sensor1.GND, Mod2.-

custom parts:
  ESP32-S3 supermini: Esp32-S3 Development board ESP32 SuperMini development board ESP32 Development board WiFi Bluetooth.
  Buzzer 12mm: Buzzer 12mm Spark Fun Electronics SKU : Comp-Buzzer Through hole This is a small 12mm round speaker that operates around the audible 2kHz range. You can use these speakers to create simple music or user interfaces. This is not a true piezoelectric speaker but behaves similarly. Instead of a piezoelectric crystal that vibrates with an electric current, this tiny speaker uses an electromagnet to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
  TTP223B Capacitive Touch Sensor Module: The TTP223B capacitive touch sensor module uses the TTP223B IC. The appropriate voltage is approximately 2 to 5.5 volts.
  KY-015 Temperature & Humidity Sensor Module: KY-015 temperature and humidity sensor module, provides a low-latency serial interface to measure humidity and temperature.
